# Fritzing sketch wiring-h-bridge (saved by Fritzing 0.9.3b)
breadboards: 1

parts:
  Súčiastka1 = Arduino Nano (Rev3.0)
  U3 = 7-SEGMENT-4DIGIT [package=7-segment-4digit-youngsun]
  SW1 = ENCODER_RGB_CA [package=encoder_led_3]
  M2 = RioRand LM2596
  J1 = Power Jack [package=power_jack_smd]
  S1 = SWITCH-MOMENTARY-2 [package=tactile-pth-12mm]
  S2 = SWITCH-MOMENTARY-2 [package=tactile-pth-12mm]
  S3 = SWITCH-MOMENTARY-2 [package=tactile-pth-12mm]
  S4 = SWITCH-MOMENTARY-2 [package=tactile-pth-12mm]
  S5 = SWITCH-MOMENTARY-2 [package=tactile-pth-12mm]
  S6 = SWITCH-MOMENTARY-2 [package=tactile-pth-12mm]
  S7 = SPST Switch [package=r_sw_th]
  M3 = DC Motor  # not connected
  F1 = FUSE [package=fuse_5mm]

nets:
  N1: Súčiastka1.D2, SW1.A
  N2: Súčiastka1.D3, SW1.+
  N3: Súčiastka1.D4, U3.14
  N4: Súčiastka1.D5, U3.13
  N5: Súčiastka1.GND, U3.15, SW1.B, M2.Pin_4, S1.2, S2.2, S3.2, S4.2, S5.2, S6.2
  N6: Súčiastka1.5V, U3.16, SW1.C, M2.Pin_3
  N7: Súčiastka1.A5, S6.1
  N8: Súčiastka1.A4, S1.1
  N9: Súčiastka1.A3, S2.1
  N10: Súčiastka1.A2, S3.1
  N11: Súčiastka1.A1, S4.1
  N12: Súčiastka1.A0, S5.1
  N13: M2.Pin_1, S7.P
  N14: M2.Pin_2, J1.GND
  N15: J1.GNDBREAK, F1.1
  N16: S7.O, F1.2

notes:
  12V
  5V
  White - CLK
  Gray - DIO
