# Fritzing sketch wiring-ubridge (saved by Fritzing 0.9.3b)
breadboards: 1

parts:
  Súčiastka1 = Arduino Nano (Rev3.0)
  U3 = 7-SEGMENT-4DIGIT [package=7-segment-4digit-youngsun]
  M2 = RioRand LM2596
  J1 = Power Jack [package=power_jack_smd]
  S1 = SWITCH-MOMENTARY-2 [package=tactile-pth-12mm]
  S2 = SWITCH-MOMENTARY-2 [package=tactile-pth-12mm]
  S3 = SWITCH-MOMENTARY-2 [package=tactile-pth-12mm]
  S4 = SWITCH-MOMENTARY-2 [package=tactile-pth-12mm]
  S5 = SWITCH-MOMENTARY-2 [package=tactile-pth-12mm]
  S6 = SWITCH-MOMENTARY-2 [package=tactile-pth-12mm]
  S7 = SPST Switch [package=r_sw_th]
  M3 = DC Motor  # not connected
  F1 = FUSE [package=fuse_5mm]
  HC-SR04_Sensor_2 = HC-SR04 Ultrasonic Distance Sensor

nets:
  N1: Súčiastka1.D2, HC-SR04_Sensor_2.TRIG
  N2: Súčiastka1.D3, HC-SR04_Sensor_2.ECHO
  N3: Súčiastka1.D4, U3.14
  N4: Súčiastka1.D5, U3.13
  GND: Súčiastka1.GND, U3.15, M2.Pin_4, S1.2, S2.2, S3.2, S4.2, S5.2, S6.2, HC-SR04_Sensor_2.GND
  5V: Súčiastka1.5V, U3.16, M2.Pin_3, HC-SR04_Sensor_2.VCC
  N5: Súčiastka1.A5, S6.1
  N6: Súčiastka1.A4, S1.1
  N7: Súčiastka1.A3, S2.1
  N8: Súčiastka1.A2, S3.1
  N9: Súčiastka1.A1, S4.1
  N10: Súčiastka1.A0, S5.1
  N11: M2.Pin_1, S7.P
  N12: M2.Pin_2, J1.GND
  N13: J1.GNDBREAK, F1.1
