# Fritzing sketch wiring-urelay (saved by Fritzing 0.9.3b)
breadboards: 1

parts:
  Súčiastka1 = Arduino Nano (Rev3.0)
  U3 = 7-SEGMENT-4DIGIT [package=7-segment-4digit-youngsun]
  U7 = G3VM-61E1 [package=g3vm-61e1]
  U8 = G3VM-61E1 [package=g3vm-61e1]
  U9 = G3VM-61E1 [package=g3vm-61e1]
  M1 = DC Motor
  M2 = RioRand LM2596
  J1 = Power Jack [package=power_jack_smd]
  S1 = SWITCH-MOMENTARY-2 [package=tactile-pth-12mm]
  S2 = SWITCH-MOMENTARY-2 [package=tactile-pth-12mm]
  S3 = SWITCH-MOMENTARY-2 [package=tactile-pth-12mm]
  S4 = SWITCH-MOMENTARY-2 [package=tactile-pth-12mm]
  S5 = SWITCH-MOMENTARY-2 [package=tactile-pth-12mm]
  S6 = SWITCH-MOMENTARY-2 [package=tactile-pth-12mm]
  S7 = SPST Switch [package=r_sw_th]
  F2 = FUSE [package=fuse_5mm]
  HC-SR04_Sensor_1 = HC-SR04 Ultrasonic Distance Sensor

nets:
  N1: Súčiastka1.D2, HC-SR04_Sensor_1.TRIG
  N2: Súčiastka1.D3, HC-SR04_Sensor_1.ECHO
  N3: Súčiastka1.D4, U3.14
  N4: Súčiastka1.D5, U3.13
  N5: Súčiastka1.D6, U8.P$6, U9.P$6
  N6: Súčiastka1.D7, U7.P$6
  GND: Súčiastka1.GND, U3.15, U7.P$5, U8.P$5, U9.P$5, M2.Pin_4, S1.2, S2.2, S3.2, S4.2, S5.2, S6.2, HC-SR04_Sensor_1.GND
  5V: Súčiastka1.5V, U3.16, U7.P$4, U8.P$4, U9.P$4, M2.Pin_3, HC-SR04_Sensor_1.VCC
  N7: Súčiastka1.A5, S6.1
  N8: Súčiastka1.A4, S1.1
  N9: Súčiastka1.A3, S2.1
  N10: Súčiastka1.A2, S3.1
  N11: Súčiastka1.A1, S4.1
  N12: Súčiastka1.A0, S5.1
  N13: U7.P$1, S7.O, F2.1
  N14: U7.P$2, U8.P$3, U9.P$1
  N15: U8.P$1, U9.P$3, M2.Pin_2, J1.GNDBREAK
  N16: U8.P$2, M1.pin_1
  N17: U9.P$2, M1.pin_2
  N18: M2.Pin_1, S7.P
