# Fritzing sketch wiring-relay (saved by Fritzing 0.9.3b)
breadboards: 1

parts:
  Súčiastka1 = Arduino Nano (Rev3.0)
  U3 = 7-SEGMENT-4DIGIT [package=7-segment-4digit-youngsun]
  SW1 = ENCODER_RGB_CA [package=encoder_led_3]
  U7 = G3VM-61E1 [package=g3vm-61e1]
  U8 = G3VM-61E1 [package=g3vm-61e1]
  U9 = G3VM-61E1 [package=g3vm-61e1]
  M1 = DC Motor
  M2 = RioRand LM2596
  J1 = Power Jack [package=power_jack_smd]
  S1 = SWITCH-MOMENTARY-2 [package=tactile-pth-12mm]
  S2 = SWITCH-MOMENTARY-2 [package=tactile-pth-12mm]
  S3 = SWITCH-MOMENTARY-2 [package=tactile-pth-12mm]
  S4 = SWITCH-MOMENTARY-2 [package=tactile-pth-12mm]
  S5 = SWITCH-MOMENTARY-2 [package=tactile-pth-12mm]
  S6 = SWITCH-MOMENTARY-2 [package=tactile-pth-12mm]
  S7 = SPST Switch [package=r_sw_th]
  F1 = FUSE [package=fuse_5mm]

nets:
  N1: Súčiastka1.D2, SW1.A
  N2: Súčiastka1.D3, SW1.+
  N3: Súčiastka1.D4, U3.14
  N4: Súčiastka1.D5, U3.13
  N5: Súčiastka1.D6, U8.P$6, U9.P$6
  N6: Súčiastka1.D7, U7.P$6
  N7: Súčiastka1.GND, U3.15, SW1.B, U7.P$5, U8.P$5, U9.P$5, M2.Pin_4, S1.2, S2.2, S3.2, S4.2, S5.2, S6.2
  N8: Súčiastka1.5V, U3.16, SW1.C, U7.P$4, U8.P$4, U9.P$4, M2.Pin_3
  N9: Súčiastka1.A5, S6.1
  N10: Súčiastka1.A4, S1.1
  N11: Súčiastka1.A3, S2.1
  N12: Súčiastka1.A2, S3.1
  N13: Súčiastka1.A1, S4.1
  N14: Súčiastka1.A0, S5.1
  N15: U7.P$1, J1.GND, S7.O
  N16: U7.P$2, U8.P$3, U9.P$1
  N17: U8.P$1, U9.P$3, M2.Pin_2, J1.GNDBREAK
  N18: U8.P$2, F1.1
  N19: U9.P$2, M1.pin_2
  N20: M1.pin_1, F1.2
  N21: M2.Pin_1, S7.P

notes:
  12V
  5V
  White - CLK
  Gray - DIO
